// Logisim project A1_6.circ as structural Verilog: 4 circuits, main circuit main
module main (
  output out_1,
  output [3:0] out_2
);

  wire clock_1_out;
  wire [3:0] multiplexer_1_out;
  wire [7:0] alu_1_f, multiplexer_2_out, multiplexer_3_out, multiplexer_4_out, PC_q, undriven, undriven_2,
       undriven_3;
  wire [15:0] rom_1_data;

  Register PC (.Q(PC_q), .clk(clock_1_out));  // open: D, en, clr
  Clock clock_1 (.out(clock_1_out));
  Adder adder_1 (.a(PC_q), .b(8'h1), .cin(1'b0), .cout(out_1));  // open: out
  ROM #(.dataWidth(20)) rom_1 (.addr(PC_q), .data({out_2, rom_1_data}));  // open: sel
  Multiplexer #(.width(4), .enable("false")) multiplexer_1 (
    .in0(rom_1_data[11:8]), .in1(rom_1_data[7:4]), .out(multiplexer_1_out));  // open: sel
  Registers registers_1 (
    .ReadData1(undriven), .WriteData(multiplexer_4_out), .ReadRegister1(rom_1_data[15:12]),
    .ReadData2(undriven_2), .WriteRegister(multiplexer_1_out), .ReadRegister2(rom_1_data[11:8]));  // open: RegWrite
  Multiplexer #(.width(8), .enable("false")) multiplexer_2 (
    .in0(undriven), .in1(undriven_2), .out(multiplexer_2_out));  // open: sel
  Multiplexer #(.select(2), .width(8), .enable("false")) multiplexer_3 (
    .in0(undriven_2), .in1({4'b0000, rom_1_data[3:0]}), .in2(rom_1_data[7:0]), .in3({8{1'b0}}),
    .out(multiplexer_3_out));  // open: sel
  Multiplexer #(.width(8), .enable("false")) multiplexer_4 (
    .in0(alu_1_f), .in1(undriven_3), .out(multiplexer_4_out));  // open: sel
  ALU alu_1 (.A(multiplexer_2_out), .B(multiplexer_3_out), .F(alu_1_f));  // open: ALUop, out_4, out_5, ZF
  DataMemory datamemory_1 (
    .Address(alu_1_f), .WriteData(undriven_2), .ReadData(undriven_3));  // open: MemWrite, MemRead, is_sp

  // Notes on the sheet:
  //   Instruction Memory
  //   Registers
  //   ALU
  //   Data Memory Unit
endmodule

module ALU (
  input  [7:0] A,
  input  [7:0] B,
  input  [2:0] ALUop,
  output out_4,
  output out_5,
  output ZF,
  output [7:0] F
);

  wire [7:0] adder_1_out, and_1_out, nor_1_out, or_1_out, subtractor_1_out;
  wire [15:0] shifter_1_out, shifter_2_out;

  Adder adder_1 (.a(A), .b(B), .out(adder_1_out), .cin(1'b0), .cout(out_4));
  Subtractor subtractor_1 (.a(A), .b(B), .out(subtractor_1_out), .bin(1'b0), .bout(out_5));
  assign or_1_out = A | B;  // OR_Gate or_1, 8 bits wide
  assign and_1_out = A & B;  // AND_Gate and_1, 8 bits wide
  assign nor_1_out = ~(A | B);  // NOR_Gate nor_1, 8 bits wide
  Shifter #(.width(16)) shifter_1 (.in({{8{1'b0}}, A}), .\dist (B[3:0]), .out(shifter_1_out));
  Shifter #(.width(16), .shift("lr")) shifter_2 (.in({{8{1'b0}}, A}), .\dist (B[3:0]), .out(shifter_2_out));
  Multiplexer #(.select(3), .width(8), .enable("false")) multiplexer_1 (
    .in0(adder_1_out), .in1(subtractor_1_out), .in2(or_1_out), .in3(and_1_out), .in4(nor_1_out),
    .in5(shifter_1_out[7:0]), .in6(shifter_2_out[7:0]), .in7({8{1'b0}}), .out(F), .sel(ALUop));
  nor nor_2 (ZF, F[0], F[1], F[2], F[3], F[4], F[5], F[6], F[7]);
endmodule

module Registers (
  input  [7:0] ReadData1,
  input  [7:0] WriteData,
  input  [3:0] ReadRegister1,
  input  RegWrite,
  input  [7:0] ReadData2,
  input  [3:0] WriteRegister,
  input  [3:0] ReadRegister2
);

  wire clock_1_out, decoder_1_out0, decoder_1_out1, decoder_1_out2, decoder_1_out3, decoder_1_out4,
       decoder_1_out5;
  wire [7:0] multiplexer_1_out, multiplexer_2_out, sp_q, t0_q, t1_q, t2_q, t3_q, t4_q, zero_q;

  Decoder #(.select(3), .disabled(0)) decoder_1 (
    .out0(decoder_1_out0), .out1(decoder_1_out1), .out2(decoder_1_out2), .out3(decoder_1_out3),
    .out4(decoder_1_out4), .out5(decoder_1_out5), .sel(WriteRegister[2:0]), .en(RegWrite));  // open: out6, out7
  Clock clock_1 (.out(clock_1_out));
  Register zero (.D(WriteData), .Q(zero_q), .clk(clock_1_out));  // open: en, clr
  Register t0 (.D(WriteData), .en(decoder_1_out0), .Q(t0_q), .clk(clock_1_out));  // open: clr
  Register t1 (.D(WriteData), .en(decoder_1_out1), .Q(t1_q), .clk(clock_1_out));  // open: clr
  Register t2 (.D(WriteData), .en(decoder_1_out2), .Q(t2_q), .clk(clock_1_out));  // open: clr
  Register t3 (.D(WriteData), .en(decoder_1_out3), .Q(t3_q), .clk(clock_1_out));  // open: clr
  Register t4 (.D(WriteData), .en(decoder_1_out4), .Q(t4_q), .clk(clock_1_out));  // open: clr
  Register sp (.D(WriteData), .en(decoder_1_out5), .Q(sp_q), .clk(clock_1_out));  // open: clr
  Multiplexer #(.select(3), .width(8), .disabled(0), .enable("false")) multiplexer_1 (
    .in0(zero_q), .in1(t0_q), .in2(t1_q), .in3(t2_q), .in4(t3_q), .in5(t4_q), .in6(sp_q), .in7({8{1'b0}}),
    .out(multiplexer_1_out), .sel(ReadRegister1[2:0]));
  Multiplexer #(.select(3), .width(8), .disabled(0), .enable("false")) multiplexer_2 (
    .in0(zero_q), .in1(t0_q), .in2(t1_q), .in3(t2_q), .in4(t3_q), .in5(t4_q), .in6(sp_q), .in7({8{1'b0}}),
    .out(multiplexer_2_out), .sel(ReadRegister2[2:0]));
endmodule

module DataMemory (
  input  [7:0] Address,
  input  [7:0] WriteData,
  input  [7:0] ReadData,
  input  MemWrite,
  input  MemRead,
  input  is_sp
);

  wire not_1_out;
  wire [7:0] multiplexer_1_out, ram_1_data, ram_2_data;

  not not_1 (not_1_out, is_sp);
  RAM #(.bus("separate")) ram_1 (
    .addr(Address), .din(WriteData), .data(ram_1_data), .str(MemWrite), .sel(not_1_out), .ld(MemRead));  // open: clk, clr
  RAM #(.bus("separate")) ram_2 (
    .addr(Address), .din(WriteData), .data(ram_2_data), .str(MemWrite), .sel(is_sp), .ld(MemRead));  // open: clk, clr
  Multiplexer #(.width(8), .disabled(0), .enable("false")) multiplexer_1 (
    .in0(ram_1_data), .in1(ram_2_data), .out(multiplexer_1_out), .sel(not_1_out));

  // Notes on the sheet:
  //   Data Memory
  //   Stack Memory
endmodule
